# Fritzing sketch one-button-to-zoom (saved by Fritzing 0.9.2b)
breadboards: 1

parts:
  Digispark1 = Digispark
  S2 = Round Pushbutton
  Button_LED = LED - 5mm [color="Red (633nm)" package="5 mm [THT]"]
  R2 = Resistor [tolerance=±5% resistance=10k package=THT]
  R1 = Resistor [tolerance=±5% resistance=220 package=THT]

nets:
  N1: Digispark1.VCC, S2.leg1, Button_LED.anode
  N2: Digispark1.GND, R2.Pin_0
  N3: Digispark1.P1, R1.Pin_0
  N4: Digispark1.P2, S2.leg0, R2.Pin_1
  N5: Button_LED.cathode, R1.Pin_1

custom parts:
  Digispark: The Digispark is an Attiny85 based microcontroller development board similar to the Arduino line, only cheaper, smaller, and a bit less powerful. With a whole host of shields to extend its functionality and the ability to use the familiar Arduino IDE the Digispark is a great way to jump into electronics, or perfect for when an Arduino is too big or too much.
